// Logisim project cpu.circ as structural Verilog: 7 circuits, main circuit main
module main (
);

  wire and_1_out, and_2_out, buffer_1_out, buffer_2_out, button_1_out, clock_1_out, core_1_write_enable;
  wire [15:0] core_1_address, core_1_data_out, ram_1_dout;

  buf buffer_1 (buffer_1_out, and_1_out);
  buf buffer_2 (buffer_2_out, buffer_1_out);
  and and_1 (and_1_out, clock_1_out, core_1_write_enable);
  RAM #(.addrWidth(16), .dataWidth(16), .trigger("high"), .databus("bibus")) ram_1 (
    .addr(core_1_address), .we(and_2_out), .din(core_1_data_out), .dout(ram_1_dout));  // open: oe
  and and_2 (and_2_out, ~and_1_out, buffer_2_out);  // AND_Gate
  Clock clock_1 (.out(clock_1_out));
  Button button_1 (.out(button_1_out));
  core core_1 (
    .data_in(ram_1_dout), .reset(button_1_out), .data_out(core_1_data_out), .address(core_1_address),
    .write_enable(core_1_write_enable));
  Clock clock_2 ();  // open: out
endmodule

module core (
  input  [15:0] data_in,
  input  reset,
  output [15:0] data_out,
  output [15:0] address,
  output write_enable
);

  wire alu_1_branch, clock_1_out, clock_2_out, inst_decode_1_alu_nand, inst_decode_1_beq, inst_decode_1_jalr,
       inst_decode_1_lwm, inst_decode_1_use_imm, nor_1_out;
  wire [2:0] inst_decode_1_ra, inst_decode_1_rb, inst_decode_1_rc;
  wire [15:0] alu_1_result, controlled_buffer_1_out, inst_decode_1_immediate, multiplexer_1_out,
       multiplexer_2_out, pc_1_pc, register_1_q, register_2_q, register_file_1_a;

  Register #(.width(16)) register_1 (.D(data_in), .en(1'b1), .clk(clock_1_out), .Q(register_1_q), .clr(reset));
  Clock clock_1 (.out(clock_1_out));
  inst_decode inst_decode_1 (
    .instruction(register_1_q), .rA(inst_decode_1_ra), .rB(inst_decode_1_rb), .rC(inst_decode_1_rc),
    .immediate(inst_decode_1_immediate), .use_imm(inst_decode_1_use_imm), .alu_nand(inst_decode_1_alu_nand),
    .lwm(inst_decode_1_lwm), .swm(write_enable), .beq(inst_decode_1_beq), .jalr(inst_decode_1_jalr));
  assign controlled_buffer_1_out = inst_decode_1_lwm ? data_in : 16'bz;  // Controlled_Buffer controlled_buffer_1
  nor nor_1 (nor_1_out, inst_decode_1_jalr, inst_decode_1_lwm);
  register_file register_file_1 (
    .data(controlled_buffer_1_out), .write(inst_decode_1_ra), .read_a(inst_decode_1_rb),
    .read_b(inst_decode_1_rc), .reset(reset), .a(register_file_1_a), .b(data_out));
  Multiplexer #(.width(16), .enable("false")) multiplexer_1 (
    .in0(data_out), .in1(inst_decode_1_immediate), .out(multiplexer_1_out), .sel(inst_decode_1_use_imm));
  assign controlled_buffer_1_out = nor_1_out ? alu_1_result : 16'bz;  // Controlled_Buffer controlled_buffer_2
  alu alu_1 (
    .a(register_file_1_a), .b(multiplexer_1_out), .alu_nand(inst_decode_1_alu_nand),
    .alu_equal(inst_decode_1_beq), .result(alu_1_result), .branch(alu_1_branch));
  assign controlled_buffer_1_out = inst_decode_1_jalr ? pc_1_pc : 16'bz;  // Controlled_Buffer controlled_buffer_3
  Multiplexer #(.width(16), .enable("false")) multiplexer_2 (
    .in0(alu_1_result), .in1(inst_decode_1_immediate), .out(multiplexer_2_out), .sel(alu_1_branch));
  Register #(.width(16), .trigger("falling")) register_2 (
    .D(pc_1_pc), .en(1'b1), .clk(clock_2_out), .Q(register_2_q), .clr(reset));
  pc pc_1 (
    .address(multiplexer_2_out), .jalr(inst_decode_1_jalr), .branch(alu_1_branch), .pc_prev(register_2_q),
    .pc(pc_1_pc));
  Clock clock_2 (.out(clock_2_out));
  Multiplexer #(.width(16), .enable("false")) multiplexer_3 (
    .in0(register_2_q), .in1(alu_1_result), .out(address), .sel(clock_2_out));
endmodule

module inst_decode (
  input  [15:0] instruction,
  output [2:0] rA,
  output [2:0] rB,
  output [2:0] rC,
  output [15:0] immediate,
  output use_imm,
  output alu_nand,
  output lwm,
  output swm,
  output beq,
  output jalr
);

  wire decoder_1_out1, decoder_1_out3, not_1_out, or_1_out, or_2_out;
  wire [15:0] bit_extender_1_out;

  Decoder #(.select(3), .enable("false")) decoder_1 (
    .out1(decoder_1_out1), .out2(alu_nand), .out3(decoder_1_out3), .out4(lwm), .out5(swm), .out6(beq),
    .out7(jalr), .sel(instruction[15:13]));  // open: out0
  assign rA = not_1_out ? instruction[12:10] : 3'bz;  // Controlled_Buffer controlled_buffer_1
  not not_1 (not_1_out, or_1_out);
  Multiplexer #(.width(3), .enable("false")) multiplexer_1 (
    .in0(instruction[6:4]), .in1(instruction[12:10]), .out(rC), .sel(or_1_out));
  or or_1 (or_1_out, swm, beq);
  assign bit_extender_1_out = {{9{instruction[6]}}, instruction[6:0]};  // Bit_Extender bit_extender_1
  or or_2 (or_2_out, decoder_1_out1, jalr, lwm, swm);
  Multiplexer #(.width(16), .enable("false")) multiplexer_2 (
    .in0(bit_extender_1_out), .in1({instruction[9:0], {6{1'b0}}}), .out(immediate), .sel(decoder_1_out3));
  or or_3 (use_imm, decoder_1_out3, or_2_out);

  assign rB = instruction[9:7];
endmodule

module register_file (
  input  [15:0] data,
  input  [2:0] write,
  input  [2:0] read_a,
  input  [2:0] read_b,
  input  reset,
  output [15:0] a,
  output [15:0] b
);

  wire clock_1_out, decoder_1_out1, decoder_1_out2, decoder_1_out3, decoder_1_out4, decoder_1_out5,
       decoder_1_out6, decoder_1_out7;
  wire [15:0] register_1_q, register_2_q, register_3_q, register_4_q, register_5_q, register_6_q,
       register_7_q;

  Decoder #(.select(3), .enable("false")) decoder_1 (
    .out1(decoder_1_out1), .out2(decoder_1_out2), .out3(decoder_1_out3), .out4(decoder_1_out4),
    .out5(decoder_1_out5), .out6(decoder_1_out6), .out7(decoder_1_out7), .sel(write));  // open: out0
  Register #(.width(16), .trigger("falling")) register_1 (
    .D(data), .en(decoder_1_out1), .clk(clock_1_out), .Q(register_1_q), .clr(reset));
  Register #(.width(16), .trigger("falling")) register_2 (
    .D(data), .en(decoder_1_out2), .clk(clock_1_out), .Q(register_2_q), .clr(reset));
  Register #(.width(16), .trigger("falling")) register_3 (
    .D(data), .en(decoder_1_out3), .clk(clock_1_out), .Q(register_3_q), .clr(reset));
  Register #(.width(16), .trigger("falling")) register_4 (
    .D(data), .en(decoder_1_out4), .clk(clock_1_out), .Q(register_4_q), .clr(reset));
  Register #(.width(16), .trigger("falling")) register_5 (
    .D(data), .en(decoder_1_out5), .clk(clock_1_out), .Q(register_5_q), .clr(reset));
  Register #(.width(16), .trigger("falling")) register_6 (
    .D(data), .en(decoder_1_out6), .clk(clock_1_out), .Q(register_6_q), .clr(reset));
  Register #(.width(16), .trigger("falling")) register_7 (
    .D(data), .en(decoder_1_out7), .clk(clock_1_out), .Q(register_7_q), .clr(reset));
  Clock clock_1 (.out(clock_1_out));
  Multiplexer #(.select(3), .width(16), .enable("false")) multiplexer_1 (
    .in0({16{1'b0}}), .in1(register_1_q), .in2(register_2_q), .in3(register_3_q), .in4(register_4_q),
    .in5(register_5_q), .in6(register_6_q), .in7(register_7_q), .out(a), .sel(read_a));
  Multiplexer #(.select(3), .width(16), .enable("false")) multiplexer_2 (
    .in0({16{1'b0}}), .in1(register_1_q), .in2(register_2_q), .in3(register_3_q), .in4(register_4_q),
    .in5(register_5_q), .in6(register_6_q), .in7(register_7_q), .out(b), .sel(read_b));
endmodule

module alu (
  input  [15:0] a,
  input  [15:0] b,
  input  alu_nand,
  input  alu_equal,
  output [15:0] result,
  output branch
);

  wire comparator_1_eq;
  wire [15:0] adder_1_out, nand_1_out;

  Adder #(.width(16)) adder_1 (.a(b), .b(a), .out(adder_1_out));  // open: cin, cout
  assign nand_1_out = ~(b & a);  // NAND_Gate nand_1, 16 bits wide
  Comparator #(.width(16)) comparator_1 (.a(b), .b(a), .eq(comparator_1_eq));  // open: gt, lt
  Multiplexer #(.width(16), .enable("false")) multiplexer_1 (
    .in0(adder_1_out), .in1(nand_1_out), .out(result), .sel(alu_nand));
  and and_1 (branch, comparator_1_eq, alu_equal);
endmodule

module pc (
  input  [15:0] address,
  input  jalr,
  input  branch,
  input  [15:0] pc_prev,
  output [15:0] pc
);

  wire nor_1_out, not_1_out;
  wire [15:0] controlled_buffer_1_out, controlled_buffer_2_out;

  assign controlled_buffer_1_out = branch ? address : 16'bz;  // Controlled_Buffer controlled_buffer_1
  nor nor_1 (nor_1_out, jalr, branch);
  assign controlled_buffer_2_out = not_1_out ? pc_prev : 16'bz;  // Controlled_Buffer controlled_buffer_2
  not not_1 (not_1_out, jalr);
  Pull_Resistor pull_resistor_1 (.node(controlled_buffer_1_out));
  Adder #(.width(16)) adder_1 (
    .a(controlled_buffer_1_out), .b(controlled_buffer_2_out), .out(pc), .cin(nor_1_out));  // open: cout
  Pull_Resistor pull_resistor_2 (.node(controlled_buffer_2_out));
endmodule

module cache (
  input  [15:0] in_1
);

  wire [7:0] ram_2_dout;

  RAM #(.dataWidth(16), .databus("bibus")) ram_1 (.addr(in_1[7:0]));  // open: we, oe, clk, din, dout
  RAM #(.addrWidth(4), .databus("bibus")) ram_2 (
    .addr(in_1[7:4]), .din(in_1[15:8]), .dout(ram_2_dout));  // open: we, oe, clk
  Comparator comparator_1 (.a(ram_2_dout), .b(in_1[15:8]));  // open: gt, eq, lt
  Counter #(.width(4), .max('hf)) counter_1 ();  // open: load, D, count, Q, carry, clk, clr
endmodule
